// Logisim project basic_gates.circ as structural Verilog: 1 circuit, main circuit main
module main (
  input  in_1,
  input  in_2,
  input  in_3,
  input  in_4,
  input  in_5,
  input  in_6,
  input  in_7,
  input  in_8,
  input  in_9,
  output out_10,
  output out_11,
  output out_12,
  output out_13,
  output out_14
);

  wire and_1_out, nor_1_out, nor_4_out, nor_5_out, or_1_out;

  and and_1 (and_1_out, in_4, in_5);
  nor nor_1 (nor_1_out, in_8, in_9);
  nor nor_2 (out_10, in_2, in_2);
  LED led_1 (.in(out_12));
  not not_1 (out_12, and_1_out);
  nor nor_3 (out_14, nor_1_out, nor_1_out);
  LED led_2 (.in(out_10));
  LED led_3 (.in(out_14));
  nor nor_4 (nor_4_out, in_6, in_6);
  nor nor_5 (nor_5_out, in_7, in_7);
  or or_1 (or_1_out, in_1, in_3);
  not not_2 (out_11, or_1_out);
  LED led_4 (.in(out_11));
  LED led_5 (.in(out_13));
  nor nor_6 (out_13, nor_4_out, nor_5_out);

  // Notes on the sheet:
  //   NOT gate using NOR gate
  //   NAND gate using AND GATE
  //   OR gate using NOR gate
  //   NOR gate using OR gate and NOTgate
  //   AND gate using NOR gate
endmodule
