// Logisim project half_adder.circ as structural Verilog: 1 circuit, main circuit main
module main (
  input  in_1,
  input  in_2,
  output out_3,
  output out_4
);

  xor xor_1 (out_3, in_1, in_2);
  and and_1 (out_4, in_2, in_1);
  LED led_1 (.in(out_3));
  LedBar ledbar_1 (.led1(out_3), .led5(out_4));  // open: led0, led2, led3, led4, led6, led7
  LED led_2 (.in(out_4));
endmodule
