// Logisim project full_adder.circ as structural Verilog: 1 circuit, main circuit main
module main (
  input  a,
  input  b,
  input  Cin,
  output sum,
  output out_5
);

  wire and_1_out, and_2_out, and_3_out;

  and and_1 (and_1_out, Cin, b);
  and and_2 (and_2_out, b, a);
  and and_3 (and_3_out, Cin, a);
  ExactlyOne xor_1 (.out(sum), .in0(a), .in1(b), .in2(Cin));
  LED led_1 (.in(sum));
  or Cout (out_5, and_1_out, and_2_out, and_3_out);
  LED led_2 (.in(out_5));
endmodule
